// Logisim project ram_memory.circ as structural Verilog: 1 circuit, main circuit main
module main (
  input  [7:0] in_1,
  input  in_2,
  input  in_3,
  input  [7:0] in_4
);

  wire clock_1_out;
  wire [7:0] ram_1_dout;

  Clock clock_1 (.out(clock_1_out));
  RAM ram_1 (.addr(in_1), .we(in_2), .oe(in_3), .clk(clock_1_out), .din(in_4), .dout(ram_1_dout));
  LED led_1 (.in(ram_1_dout[0]));
  LED led_2 (.in(ram_1_dout[1]));
  LED led_3 (.in(ram_1_dout[2]));
  LED led_4 (.in(ram_1_dout[3]));
  LED led_5 (.in(ram_1_dout[4]));
  LED led_6 (.in(ram_1_dout[5]));
  LED led_7 (.in(ram_1_dout[6]));
  LED led_8 (.in(ram_1_dout[7]));
endmodule
