// Logisim project registrador_si_po.circ as structural Verilog: 1 circuit, main circuit main
module main (
  input  D,
  input  Clear,
  output Qa,
  output Qb,
  output Qc,
  output Qd
);

  wire CLK_out;

  Clock CLK (.out(CLK_out));
  D_Flip_Flop d_ff_1 (.D(D), .clk(CLK_out), .Q(Qa), .reset(Clear));  // open: Qn, preset
  D_Flip_Flop d_ff_2 (.D(Qa), .clk(CLK_out), .Q(Qb), .reset(Clear));  // open: Qn, preset
  D_Flip_Flop d_ff_3 (.D(Qb), .clk(CLK_out), .Q(Qc), .reset(Clear));  // open: Qn, preset
  D_Flip_Flop d_ff_4 (.D(Qc), .clk(CLK_out), .Q(Qd), .reset(Clear));  // open: Qn, preset
endmodule
